// Logisim project control-logic.circ as structural Verilog: 3 circuits, main circuit control_logic
module control_logic (
  input  [31:0] Instruction,
  input  BrEq,
  input  BrLt,
  output PCSel,
  output RegWEn,
  output [2:0] ImmSel,
  output BrUn,
  output ASel,
  output BSel,
  output [3:0] ALUSel,
  output MemWEn,
  output [1:0] WBSel
);

  wire Iformat, MemWEN_t, not_1_out, not_2_out, not_3_out, not_4_out, not_5_out, not_6_out, not_7_out,
       not_8_out, not_9_out, not_10_out, not_11_out, not_12_out, Rformat;
  wire [3:0] i_type_func3_handler_1_alusel, Instruction_Type, r_type_alusel_handler_1_alusel;
  wire [15:0] rom_1_data;

  not not_1 (not_1_out, Instruction[2]);
  not not_2 (not_2_out, Instruction[3]);
  not not_3 (not_3_out, Instruction[5]);
  not not_4 (not_4_out, Instruction[6]);
  not not_5 (not_5_out, Instruction[2]);
  not not_6 (not_6_out, Instruction[3]);
  not not_7 (not_7_out, Instruction[6]);
  and and_1 (Iformat, not_1_out, not_2_out, Instruction[4], not_3_out, not_4_out);
  and and_2 (Rformat, not_5_out, not_6_out, Instruction[4], Instruction[5], not_7_out);
  Priority_Encoder #(.disabled("Z"), .select_enc(4)) priority_encoder_1 (
    .in0(Iformat), .in1(Rformat), .out(Instruction_Type));  // open: in2, in3, in4, in5, in6, in7, in8, in9, in10, in11, in12, in13, in14, in15, gs, en_out, en_in
  I_Type_func3_handler i_type_func3_handler_1 (
    .func3(Instruction[14:12]), .func7_bit30(Instruction[30]), .ALUSel(i_type_func3_handler_1_alusel));
  R_Type_ALUSel_Handler r_type_alusel_handler_1 (
    .func3(Instruction[14:12]), .func7(Instruction[31:25]), .ALUSel(r_type_alusel_handler_1_alusel));
  Multiplexer #(.select(4), .width(4)) multiplexer_1 (
    .in0(i_type_func3_handler_1_alusel), .in1(r_type_alusel_handler_1_alusel), .out(ALUSel),
    .sel(Instruction_Type));  // open: in2, in3, in4, in5, in6, in7, in8, in9, in10, in11, in12, in13, in14, in15
  not not_8 (not_8_out, Iformat);
  not not_9 (not_9_out, Rformat);
  not not_10 (not_10_out, Iformat);
  not not_11 (not_11_out, Rformat);
  not not_12 (not_12_out, Rformat);
  Multiplexer #(.select(4)) multiplexer_2 (
    .in0(Iformat), .in1(Rformat), .out(RegWEn), .sel(Instruction_Type));  // open: in2, in3, in4, in5, in6, in7, in8, in9, in10, in11, in12, in13, in14, in15
  Multiplexer #(.select(4)) multiplexer_3 (
    .in0(not_8_out), .in1(not_9_out), .out(MemWEN_t), .sel(Instruction_Type));  // open: in2, in3, in4, in5, in6, in7, in8, in9, in10, in11, in12, in13, in14, in15
  Multiplexer #(.select(4)) multiplexer_4 (
    .in0(not_10_out), .in1(not_11_out), .out(ASel), .sel(Instruction_Type));  // open: in2, in3, in4, in5, in6, in7, in8, in9, in10, in11, in12, in13, in14, in15
  Multiplexer #(.select(4)) multiplexer_5 (
    .in0(Iformat), .in1(not_12_out), .out(BSel), .sel(Instruction_Type));  // open: in2, in3, in4, in5, in6, in7, in8, in9, in10, in11, in12, in13, in14, in15
  ROM #(.addrWidth(6), .dataWidth(16)) rom_1 (.data(rom_1_data));  // open: addr

  // Other names for the same wires on the sheet: opcode[4:0] = Instruction[6:2]

  // Notes on the sheet:
  //   INPUTS to your circuit
  //   We only consider RV32 here so the 0 bit and 1 bit of instructions are not considered since they are all the same 
  //   0: for I-type
  //   Determine Instruction type 
  //   DON'T CHANGE THE LOCATIONS OF THE INPUTS AND OUTPUTS!
  //   OUTPUT from your circuit
  //   RegWEN
  //   MemRW
  //   ASel
  //   BSel
  //   Connect ROM Input here ->
  //   ALUSel
  //   ROM FOR CONTROL LOGIC
  //   This is only if you choose to do the ROM option
  //   CONNECT
  //   WIRE
  //   TO
  //   USE
  //   ROM
  //   Reminder: If using ROM, use combinational logic for PCSel
endmodule

module I_Type_func3_handler (
  input  [2:0] func3,
  input  func7_bit30,
  output [3:0] ALUSel
);

  wire and_1_out, not_1_out;
  wire [3:0] bit_extender_1_out;

  not not_1 (not_1_out, func3[1]);
  assign bit_extender_1_out = {{1{1'b0}}, func3};  // Bit_Extender bit_extender_1
  and and_1 (and_1_out, func3[0], not_1_out, func3[2], func7_bit30);
  Multiplexer #(.width(4)) multiplexer_1 (.in0(bit_extender_1_out), .in1(4'b1101), .out(ALUSel), .sel(and_1_out));

  // Notes on the sheet:
  //   If it is srai
endmodule

module R_Type_ALUSel_Handler (
  input  [2:0] func3,
  input  [6:0] func7,
  output [3:0] ALUSel
);

  wire [3:0] bit_extender_1_out, multiplexer_1_out, multiplexer_2_out;

  Multiplexer #(.select(2), .width(4)) multiplexer_1 (
    .in0(4'b1000), .in1(4'b1001), .in3(4'b1011), .out(multiplexer_1_out), .sel(func3[1:0]));  // open: in2
  Multiplexer #(.width(4)) multiplexer_2 (.in0(4'b1100), .in1(4'b1101), .out(multiplexer_2_out), .sel(func3[0]));
  assign bit_extender_1_out = {{1{1'b0}}, func3};  // Bit_Extender bit_extender_1
  Multiplexer #(.select(2), .width(4)) multiplexer_3 (
    .in0(bit_extender_1_out), .in1(multiplexer_1_out), .in2(multiplexer_2_out), .out(ALUSel),
    .sel({func7[5], func7[0]}));  // open: in3

  // Notes on the sheet:
  //   mul
  //   mulh
  //   mulhu
  //   sub
  //   sra
endmodule
